# Fritzing sketch TempUmidity (saved by Fritzing 0.9.3b)
circuit board: 6.88566cm x 5.36311cm
breadboards: 1

parts:
  LCD1 = LCD screen
  Contrast1 = Rotary Potentiometer (Small) [maximum_resistance=100kΩ package=THT]
  Arduino1 = Arduino Uno (Rev3)
  YwRobot_Power_Supply1 = YwRobot Breadboard Power Supply [part_number=545043]
  RHT1 = Humidity and Temperature Sensor RHT03
  part = Resistor [tolerance=±5% resistance=10k package=THT]  # not connected
  R2 = Resistor [tolerance=±5% resistance=220 package=THT]

nets (from the breadboard view):
  VSS: LCD1.VSS, LCD1.R/W, LCD1.LED-, Contrast1.leg1, Arduino1.GND, YwRobot_Power_Supply1.GND#12, RHT1.GND_2
  N1: LCD1.V0, Contrast1.wiper
  N2: LCD1.RS, Arduino1.D4
  N3: LCD1.E, Arduino1.D6_PWM
  N4: LCD1.DB4, Arduino1.D8
  N5: LCD1.DB5, Arduino1.D9_PWM
  N6: LCD1.DB6, Arduino1.D10_PWM/SS
  N7: LCD1.DB7, Arduino1.D11_PWM/MOSI
  N8: LCD1.LED+, R2.Pin_1
  N9: Contrast1.leg2, Arduino1.5V, YwRobot_Power_Supply1.VCC#6, RHT1.Data-signal, R2.Pin_0
  N10: YwRobot_Power_Supply1.VCC#10, RHT1.Vcc

custom parts:
  YwRobot Breadboard Power Supply: The YwRobot Breadboard Power Supply (MB-V2) has two power rails; they can be 5V or 3V3. Power to the module can be provided through the female USB socket or through the A10 (female) 2.1mm power jack.
